# Fritzing sketch circuit (saved by Fritzing 0.9.2b)
perfboards: 1

parts:
  J8 = female pin header, 20 pins [form="♀ (female)"]
  J10 = male pin header, 4 pins [form="♂ (male)"]
  IC2 = MCP3008 8-channel 10-bit ADC [part_number=MCP3008]
  J11 = male pin header, 8 pins [form="♂ (male)"]  # not connected
  J12 = male pin header, 8 pins [form="♂ (male)"]
  J14 = male pin header, 8 pins [form="♂ (male)"]
  R11 = Resistor [tolerance=±5% resistance=1k package=THT]
  R12 = Resistor [tolerance=±5% resistance=1k package=THT]  # not connected
  R13 = Resistor [tolerance=±5% resistance=1k package=THT]
  R14 = Resistor [tolerance=±5% resistance=1k package=THT]
  R15 = Resistor [tolerance=±5% resistance=1k package=THT]
  R16 = Resistor [tolerance=±5% resistance=1k package=THT]
  R17 = Resistor [tolerance=±5% resistance=1k package=THT]
  R18 = Resistor [tolerance=±5% resistance=1k package=THT]
  R19 = Resistor [tolerance=±5% resistance=4.7 package=THT]
  J15 = male pin header, 8 pins [form="♂ (male)"]
  J16 = male pin header, 8 pins [form="♂ (male)"]
  J13 = male pin header, 8 pins [form="♂ (male)"]
  R20 = Resistor [tolerance=±5% resistance=4.7 package=THT]
  J17 = male pin header, 8 pins [form="♂ (male)"]  # not connected
  J9 = female pin header, 20 pins [form="♀ (female)"]

nets:
  N1: J8.pin4, R11.Pin_1
  N2: J8.pin5, R14.Pin_1
  N3: J8.pin6, R17.Pin_1
  N4: J8.pin8, R13.Pin_1
  N5: J8.pin10, J13.pin8
  N6: J8.pin12, IC2.no_name_yet#10
  N7: J10.pin4, J9.pin5
  N8: IC2.no_name_yet#1, J16.pin1
  N9: IC2.no_name_yet#2, J16.pin2
  N10: IC2.no_name_yet#3, J16.pin3
  N11: IC2.no_name_yet#4, J16.pin4
  N12: IC2.no_name_yet#5, J16.pin5
  N13: IC2.no_name_yet#6, J16.pin6
  N14: IC2.no_name_yet#7, J16.pin7
  N15: IC2.no_name_yet#8, J16.pin8
  N16: IC2.no_name_yet#11, J9.pin10
  N17: IC2.no_name_yet#12, J9.pin11
  N18: IC2.no_name_yet#13, J9.pin12
  N19: IC2.no_name_yet#16, J15.pin1, J9.pin9
  N20: J12.pin1, R20.Pin_1
  N21: J14.pin7, J9.pin8
  N22: R13.Pin_0, R19.Pin_0, J9.pin1
  N23: R15.Pin_1, J9.pin4
  N24: R16.Pin_1, J9.pin6
  N25: R18.Pin_1, J9.pin7
  N26: R19.Pin_1, R20.Pin_0
