# Fritzing sketch sencors_circuit (saved by Fritzing 0.9.2b)
perfboards: 1

parts:
  IC1 = MCP3008 8-channel 10-bit ADC [part_number=MCP3008]
  Raspberry_Pi1 = Raspberry Pi 2
  J2 = male pin header, 4 pins [form="♂ (male)"]
  J1 = male pin header, 2 pins [form="♂ (male)"]
  J5 = male pin header, 8 pins [form="♂ (male)"]
  J3 = male pin header, 8 pins [form="♂ (male)"]
  J4 = male pin header, 8 pins [form="♂ (male)"]

nets:
  N1: IC1.no_name_yet#1, J4.pin1
  N2: IC1.no_name_yet#2, J4.pin2
  N3: IC1.no_name_yet#3, J4.pin3
  N4: IC1.no_name_yet#4, J4.pin4
  N5: IC1.no_name_yet#5, J4.pin5
  N6: IC1.no_name_yet#6, J4.pin6
  N7: IC1.no_name_yet#7, J4.pin7
  N8: IC1.no_name_yet#8, J4.pin8
  N9: IC1.no_name_yet#9, Raspberry_Pi1.GND, J1.pin2, J3.pin1, J3.pin2, J3.pin3, J3.pin4, J3.pin5, J3.pin6, J3.pin7, J3.pin8
  N10: IC1.no_name_yet#10, J2.pin1
  N11: IC1.no_name_yet#11, J2.pin4
  N12: IC1.no_name_yet#12, J2.pin3
  N13: IC1.no_name_yet#13, J2.pin2
  N14: IC1.no_name_yet#16, Raspberry_Pi1.3V3, J1.pin1, J5.pin1, J5.pin2, J5.pin3, J5.pin4, J5.pin5, J5.pin6, J5.pin7, J5.pin8
