# Fritzing sketch touch_2 (saved by Fritzing 0.9.2b)
perfboards: 1

parts:
  R1 = Resistor [tolerance=±5% resistance=1k package=THT]
  R2 = Resistor [tolerance=±5% resistance=1k package=THT]  # not connected
  R3 = Resistor [tolerance=±5% resistance=1k package=THT]  # not connected
  R4 = Resistor [tolerance=±5% resistance=1k package=THT]  # not connected
  R5 = Resistor [tolerance=±5% resistance=1k package=THT]  # not connected
  R6 = Resistor [tolerance=±5% resistance=1k package=THT]  # not connected
  R7 = Resistor [tolerance=±5% resistance=1k package=THT]  # not connected
  R8 = Resistor [tolerance=±5% resistance=1k package=THT]  # not connected
  LED1 = LED - 5mm [color="White (6500K)" package="5 mm [THT]"]  # not connected
  LED2 = LED - 5mm [color="Infrared (940nm)" package="5 mm [THT]"]
  Raspberry_Pi1 = Raspberry Pi 2  # not connected
  R9 = Resistor [tolerance=±5% resistance=4.7 package=THT]
  R10 = Resistor [tolerance=±5% resistance=4.7 package=THT]

nets:
  N1: R1.Pin_1, LED2.anode
  N2: R9.Pin_1, R10.Pin_0
